// Logisim project sle1_starter.circ as structural Verilog: 1 circuit, main circuit main
module main (
  input  S,
  input  R,
  output Q,
  output Q_prime
);

  nor nor_1 (Q_prime, S, Q);
  nor nor_2 (Q, Q_prime, R);

  // Notes on the sheet:
  //   Inputs
  //   Outputs
endmodule
