// Logisim project sle4_starter.circ as structural Verilog: 1 circuit, main circuit main
module main (
  input  in_1,
  output [3:0] Outputs
);

  wire and_1_out, and_2_out, and_3_out, and_4_out, and_5_out, and_6_out, and_7_out, and_8_out, and_9_out,
       and_10_out, and_11_out, and_12_out, and_13_out, and_14_out, and_15_out, and_16_out, and_17_out,
       and_18_out, and_19_out, clock_1_out, d_ff_1_q, d_ff_1_qn, d_ff_2_q, d_ff_2_qn, d_ff_3_q, d_ff_3_qn,
       d_ff_4_q, d_ff_4_qn, not_1_out, or_1_out, or_2_out, or_3_out, or_4_out;

  Clock clock_1 (.out(clock_1_out));
  or or_1 (or_1_out, and_2_out, and_1_out, and_3_out, and_4_out);
  or or_2 (or_2_out, and_5_out, and_6_out, and_7_out);
  or or_3 (or_3_out, and_8_out, and_9_out);
  or or_4 (or_4_out, and_10_out, and_11_out);
  D_Flip_Flop #(.trigger("falling")) d_ff_1 (
    .clk(clock_1_out), .D(or_1_out), .Q(d_ff_1_q), .Qn(d_ff_1_qn));  // open: preset, en, reset
  D_Flip_Flop #(.trigger("falling")) d_ff_2 (
    .clk(clock_1_out), .D(or_2_out), .Q(d_ff_2_q), .Qn(d_ff_2_qn));  // open: preset, en, reset
  D_Flip_Flop #(.trigger("falling")) d_ff_3 (
    .clk(clock_1_out), .D(or_3_out), .Q(d_ff_3_q), .Qn(d_ff_3_qn));  // open: preset, en, reset
  D_Flip_Flop #(.trigger("falling")) d_ff_4 (
    .clk(clock_1_out), .D(or_4_out), .Q(d_ff_4_q), .Qn(d_ff_4_qn));  // open: preset, en, reset
  and and_1 (and_1_out, d_ff_1_q, d_ff_2_qn, not_1_out);
  and and_2 (and_2_out, d_ff_1_q, d_ff_3_qn, not_1_out);
  not not_1 (not_1_out, in_1);
  and and_3 (and_3_out, d_ff_1_q, d_ff_3_q, d_ff_4_qn, not_1_out);
  and and_4 (and_4_out, d_ff_1_qn, d_ff_2_q, d_ff_3_q, d_ff_4_q, not_1_out);
  and and_5 (and_5_out, d_ff_2_q, d_ff_3_qn, not_1_out);
  and and_6 (and_6_out, d_ff_2_q, d_ff_3_q, d_ff_4_qn, not_1_out);
  and and_7 (and_7_out, d_ff_2_qn, d_ff_3_q, d_ff_4_q, not_1_out);
  and and_8 (and_8_out, d_ff_3_qn, d_ff_4_q, not_1_out);
  and and_9 (and_9_out, d_ff_3_q, d_ff_4_qn, not_1_out);
  and and_10 (and_10_out, d_ff_3_qn, d_ff_4_qn, not_1_out);
  and and_11 (and_11_out, d_ff_3_q, d_ff_4_qn, not_1_out);
  and and_12 (and_12_out, d_ff_1_q, d_ff_2_q);
  and and_13 (and_13_out, d_ff_1_q, d_ff_2_qn);
  and and_14 (and_14_out, d_ff_1_qn, d_ff_2_q);
  and and_15 (and_15_out, d_ff_1_q, d_ff_2_q);
  and and_16 (and_16_out, d_ff_3_q, d_ff_4_q);
  and and_17 (and_17_out, d_ff_3_q, d_ff_4_qn);
  and and_18 (and_18_out, d_ff_3_qn, d_ff_4_q);
  and and_19 (and_19_out, d_ff_3_q, d_ff_4_q);
  or or_5 (Outputs[3], and_12_out, and_13_out);
  or or_6 (Outputs[2], and_14_out, and_15_out);
  or or_7 (Outputs[1], and_16_out, and_17_out);
  or or_8 (Outputs[0], and_18_out, and_19_out);
endmodule
