// Logisim project sequential_logic_lab_2_bit_counter.circ as structural Verilog: 1 circuit, main circuit main
module main (
  output out_1,
  output out_2
);

  wire and_1_out, and_2_out, clock_1_out, d_ff_1_qn, d_ff_2_qn, or_1_out;

  Clock clock_1 (.out(clock_1_out));
  D_Flip_Flop #(.trigger("falling")) d_ff_1 (
    .clk(clock_1_out), .D(or_1_out), .Q(out_1), .Qn(d_ff_1_qn));  // open: preset, en, reset
  D_Flip_Flop #(.trigger("falling")) d_ff_2 (
    .clk(clock_1_out), .D(d_ff_2_qn), .Q(out_2), .Qn(d_ff_2_qn));  // open: preset, en, reset
  and and_1 (and_1_out, out_2, d_ff_1_qn);
  and and_2 (and_2_out, d_ff_2_qn, out_1);
  or or_1 (or_1_out, and_1_out, and_2_out);
endmodule
