// Logisim project sequential_logic_lab_3_bit_counter.circ as structural Verilog: 1 circuit, main circuit main
module main (
  output out_1,
  output out_2,
  output out_3
);

  wire and_1_out, and_2_out, and_3_out, and_4_out, and_5_out, clock_1_out, d_ff_1_qn, d_ff_2_qn, d_ff_3_qn,
       or_1_out, or_2_out;

  Clock clock_1 (.out(clock_1_out));
  D_Flip_Flop #(.trigger("falling")) d_ff_1 (
    .clk(clock_1_out), .D(or_2_out), .Q(out_1), .Qn(d_ff_1_qn));  // open: preset, en, reset
  D_Flip_Flop #(.trigger("falling")) d_ff_2 (
    .clk(clock_1_out), .D(or_1_out), .Q(out_2), .Qn(d_ff_2_qn));  // open: preset, en, reset
  D_Flip_Flop #(.trigger("falling")) d_ff_3 (
    .clk(clock_1_out), .D(d_ff_3_qn), .Q(out_3), .Qn(d_ff_3_qn));  // open: preset, en, reset
  and and_1 (and_1_out, out_3, d_ff_2_qn);
  and and_2 (and_2_out, d_ff_3_qn, out_2);
  or or_1 (or_1_out, and_1_out, and_2_out);
  and and_3 (and_3_out, out_1, d_ff_2_qn);
  and and_4 (and_4_out, out_1, d_ff_3_qn);
  or or_2 (or_2_out, and_3_out, and_4_out, and_5_out);
  and and_5 (and_5_out, d_ff_1_qn, out_2, out_3);
endmodule
